# Fritzing sketch diagram (saved by Fritzing 0.9.3b)
breadboards: 1

parts:
  Part1 = Arduino Uno (Rev3) - ICSP
  Part2 = Adafruit 1.44 inch TFT Breakout [part_number="Adafruit #2088"]
  R1 = Trimmer Potentiometer [maximum_resistance=10kΩ package=THT]
  R2 = Trimmer Potentiometer [maximum_resistance=10kΩ package=THT]
  R3 = Trimmer Potentiometer [maximum_resistance=10kΩ package=THT]
  S1 = Pushbutton [package="[THT]"]
  R4 = Resistor [tolerance=±5% resistance=10k package="0603 [SMD]"]
  S2 = Pushbutton [package="[THT]"]
  R5 = Resistor [tolerance=±5% resistance=10k package="0603 [SMD]"]

nets:
  N1: Part1.A0, R1.wiper
  N2: Part1.A1, R2.wiper
  N3: Part1.A2, R3.wiper
  N4: Part1.ICSP_MOSI, Part1.D11_PWM/MOSI, Part2.MOSI
  N5: Part1.D8, Part2.TFTDC
  N6: Part1.D9_PWM, Part2.RESET
  N7: Part1.D10_PWM/SS, Part2.TFTCS
  N8: Part1.D13/SCK, Part2.SCK
  N9: Part1.D2, S1.Pin_3, S1.Pin_4
  N10: Part1.D5_PWM, S2.Pin_3, S2.Pin_4
  5V: Part1.5V, Part2.VIN, R1.leg1, R2.leg1, R3.leg1
  GND: Part1.GND, Part2.GND, R1.leg2, R2.leg2, R3.leg2, R4.Pin_1, R5.Pin_1
  N11: S1.Pin_1, S1.Pin_2, R4.Pin_0
  N12: S2.Pin_1, S2.Pin_2, R5.Pin_0

custom parts:
  Adafruit 1.44 inch TFT Breakout: This lovely little display breakout is the best way to add a small, colorful and bright display to any project. Since the display uses 4-wire SPI to communicate and has its own pixel-addressable frame buffer, it can be used with every kind of microcontroller. Even a very small one with low memory and few pins available! The 1.44" display has 128x128 color pixels. Unlike the low cost "Nokia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
